# Fritzing sketch openbot-diy-power-hub (saved by Fritzing 1.0.8)

parts:
  BAT1_·_аккумуляторная_батарея = 3 × 18650 · 3S
  SW1_·_ON/OFF_с_фиксацией = SW1 · питание
  Распределитель_·_Nano_/_L298N = Распределитель питания Nano / L298N
  R1_·_20_кОм = R1
  R2_·_10_кОм = R2
  L298N_·_+12V_/_GND_/_5V = L298N · три линии питания
  heading = heading  # not connected
  switch_caption = switch_caption  # not connected
  legend = legend  # not connected

nets:
  N1: BAT1_·_аккумуляторная_батарея.+, SW1_·_ON/OFF_с_фиксацией.IN, SW1_·_ON/OFF_с_фиксацией.OUT, Распределитель_·_Nano_/_L298N.BAT+, Распределитель_·_Nano_/_L298N.SW_IN, Распределитель_·_Nano_/_L298N.SW_OUT, Распределитель_·_Nano_/_L298N.VBAT_L298N, Распределитель_·_Nano_/_L298N.VBAT_R1, R1_·_20_кОм.1, L298N_·_+12V_/_GND_/_5V.+12V
  GND: BAT1_·_аккумуляторная_батарея.GND, Распределитель_·_Nano_/_L298N.GND_BAT, Распределитель_·_Nano_/_L298N.GND_L298N, Распределитель_·_Nano_/_L298N.GND_OLED, Распределитель_·_Nano_/_L298N.GND_HC-SR04, Распределитель_·_Nano_/_L298N.GND_FC-03_L, Распределитель_·_Nano_/_L298N.GND_FC-03_R, Распределитель_·_Nano_/_L298N.GND_NANO, Распределитель_·_Nano_/_L298N.GND_R2, R2_·_10_кОм.2, L298N_·_+12V_/_GND_/_5V.GND
  N2: Распределитель_·_Nano_/_L298N.5V_L298N, Распределитель_·_Nano_/_L298N.5V_OLED, Распределитель_·_Nano_/_L298N.5V_HC-SR04, Распределитель_·_Nano_/_L298N.5V_FC-03_L, Распределитель_·_Nano_/_L298N.5V_FC-03_R, L298N_·_+12V_/_GND_/_5V.5V
  N3: Распределитель_·_Nano_/_L298N.A7_NANO, R1_·_20_кОм.2, R2_·_10_кОм.1

custom parts:
  3 × 18650 · 3S: OpenBot DIY: bundled Fritzing library artwork adapted to the existing connector IDs. Original author and license: library-parts/sources.json. See README.breadboard.ru-RU.md. Source: https://forum.fritzing.org/t/18650-battery-holder-part-design/6523/32; Published Fritzing part; no explicit license in FZP
  SW1 · питание: OpenBot DIY: bundled Fritzing library artwork adapted to the existing connector IDs. Original author and license: library-parts/sources.json. See README.breadboard.ru-RU.md. Source: https://github.com/fritzing/fritzing-parts/blob/develop/core/basic-toggle-switch.fzp; CC BY-SA 3.0
  Распределитель питания Nano / L298N: OpenBot detachable power module wiring. CC BY-SA 3.0. Artwork credits: Fritzing core, Peter Van Epp. Wiring and layout only; no manufacturing PCB view.
  R1: OpenBot DIY: bundled Fritzing library artwork adapted to the existing connector IDs. Original author and license: library-parts/sources.json. See README.breadboard.ru-RU.md. Source: https://github.com/fritzing/fritzing-parts/blob/develop/core/resistor.fzp; CC BY-SA 3.0
  R2: OpenBot DIY: bundled Fritzing library artwork adapted to the existing connector IDs. Original author and license: library-parts/sources.json. See README.breadboard.ru-RU.md. Source: https://github.com/fritzing/fritzing-parts/blob/develop/core/resistor.fzp; CC BY-SA 3.0
  L298N · три линии питания: OpenBot detachable power module wiring. CC BY-SA 3.0. Artwork credits: Fritzing core, Peter Van Epp. Wiring and layout only; no manufacturing PCB view.
  heading: OpenBot detachable power module wiring. CC BY-SA 3.0. Artwork credits: Fritzing core, Peter Van Epp. Wiring and layout only; no manufacturing PCB view.
  switch_caption: OpenBot detachable power module wiring. CC BY-SA 3.0. Artwork credits: Fritzing core, Peter Van Epp. Wiring and layout only; no manufacturing PCB view.
  legend: OpenBot detachable power module wiring. CC BY-SA 3.0. Artwork credits: Fritzing core, Peter Van Epp. Wiring and layout only; no manufacturing PCB view.
